# Fritzing sketch leonardo (saved by Fritzing 0.8.7b)

parts:
  Parte1 = Arduino Leonardo (Rev3b)
  Parte3 = Arduino XBee Shield

nets:
  N1: Parte1.D0/RX, Parte3.UART_RX
  N2: Parte1.D1/TX, Parte3.UART_TX
  N3: Parte1.D2/SDA, Parte3.D_RX
  N4: Parte1.D3_PWM/SCL, Parte3.D_TX
  N5: Parte1.D4/A6, Parte3.D4
  N6: Parte1.D5_PWM, Parte3.D5
  N7: Parte1.D6_PWM/A7, Parte3.D6
  N8: Parte1.D7, Parte3.D7
  N9: Parte1.RESET, Parte3.RST
  5V: Parte1.5V, Parte3.5V
  GND: Parte1.GND, Parte3.GND
  VIN: Parte1.VIN, Parte3.VIN
  N10: Parte1.A0, Parte3.A0
  N11: Parte1.A1, Parte3.A1
  N12: Parte1.A2, Parte3.A2
  N13: Parte1.A3, Parte3.A3
  N14: Parte1.A4, Parte3.A4
  N15: Parte1.A5, Parte3.A5
  N16: Parte1.D8/A8, Parte3.D8
  N17: Parte1.D9_PWM/A9, Parte3.D9
  N18: Parte1.D10_PWM/A10, Parte3.D10
  N19: Parte1.D11_PWM, Parte3.D11
  N20: Parte1.D12/A11, Parte3.D12
  N21: Parte1.D13_PWM, Parte3.D13
  N22: Parte1.AREF, Parte3.AREF
